// Logisim project P.F.C_projet_E.S.circ as structural Verilog: 1 circuit, main circuit main
module main (
  input  pierre,
  input  feuille,
  input  ciseaux,
  input  pierre_2,
  input  feuille_2,
  input  ciseaux_2,
  output joueur_1,
  output joueur_2
);

  wire and_1_out, and_2_out, and_3_out, and_4_out, and_5_out, and_6_out, and_7_out, and_8_out, and_9_out,
       or_1_out;

  and and_1 (and_1_out, pierre, ciseaux_2);
  and and_2 (and_2_out, feuille, pierre_2);
  and and_3 (and_3_out, ciseaux, feuille_2);
  and and_4 (and_4_out, pierre, pierre_2);
  and and_5 (and_5_out, feuille, feuille_2);
  and and_6 (and_6_out, ciseaux, ciseaux_2);
  and and_7 (and_7_out, pierre, feuille_2);
  and and_8 (and_8_out, feuille, ciseaux_2);
  and and_9 (and_9_out, ciseaux, pierre_2);
  or or_1 (or_1_out, and_4_out, and_5_out, and_6_out);
  or or_2 (joueur_1, and_1_out, and_2_out, and_3_out, or_1_out);
  or or_3 (joueur_2, or_1_out, and_7_out, and_8_out, and_9_out);
endmodule
